# Fritzing sketch circuit_layout (saved by Fritzing 1.0.0rc)
breadboards: 1

parts:
  Bela1 = Bela
  Trill_Craft1 = Trill Craft
  Accelerometer_Left_Hand = Triple Axis Accelerometer Breakout - ADXL335
  Accelerometer_Right_Hand = Triple Axis Accelerometer Breakout - ADXL335
  Capacitive_Sensor_1 = Antenna
  Button_1_left_hand = Momentary Switch [package=ksa_sealed_tac_switch]
  Capacitive_Sensor_2 = Antenna
  Capacitive_Sensor_3 = Antenna
  Capacitive_Sensor_4 = Antenna
  Capacitive_Sensor_5 = Antenna
  Capacitive_Sensor_6 = Antenna
  Capacitive_Sensor_7 = Antenna
  Capacitive_Sensor_8 = Antenna
  Capacitive_Sensor_9 = Antenna
  Capacitive_Sensor_10 = Antenna
  Capacitive_Sensor_12 = Antenna
  Capacitive_Sensor_11 = Antenna
  Capacitive_Sensor_13 = Antenna
  Capacitive_Sensor_14 = Antenna
  Capacitive_Sensor_15 = Antenna
  Capacitive_Sensor_16 = Antenna
  R2 = Resistor [tolerance=±5% resistance=10k power=0.25W package=THT]
  LED4_right_hand = smd LED [color="Red (633nm)" package="1206 [SMD]"]
  R3 = Resistor [tolerance=±5% resistance=220 power=0.25W package=THT]
  R4 = Resistor [tolerance=±5% resistance=10k power=0.25W package=THT]
  Button_2_left_hand = Momentary Switch [package=ksa_sealed_tac_switch]
  LED3_right_hand = smd LED [color="Red (633nm)" package="1206 [SMD]"]
  R5 = Resistor [tolerance=±5% resistance=220 power=0.25W package=THT]
  LED2_left_hand = smd LED [color="Red (633nm)" package="1206 [SMD]"]
  LED1_left_hand = smd LED [color="Red (633nm)" package="1206 [SMD]"]
  R6 = Resistor [tolerance=±5% resistance=220 power=0.25W package=THT]
  R7 = Resistor [tolerance=±5% resistance=220 power=0.25W package=THT]
  R8 = Resistor [tolerance=±5% resistance=10k power=0.25W package=THT]
  R9 = Resistor [tolerance=±5% resistance=10k power=0.25W package=THT]
  Button_1_right_hand = Momentary Switch [package=ksa_sealed_tac_switch]
  Button_2_right_hand = Momentary Switch [package=ksa_sealed_tac_switch]

nets:
  N1: Bela1.P8_01_GND, R2.Pin_0, R3.Pin_1, R4.Pin_0, R5.Pin_1, R6.Pin_1, R7.Pin_1, R8.Pin_0, R9.Pin_0
  N2: Bela1.P8_07_D0, LED1_left_hand.anode
  N3: Bela1.P8_08_D1, LED2_left_hand.anode
  N4: Bela1.P8_09_D2, LED3_right_hand.anode
  N5: Bela1.P8_10_D3, LED4_right_hand.anode
  N6: Bela1.P8_11_D4, Button_1_left_hand.1, R2.Pin_1
  N7: Bela1.P8_12_D5, R4.Pin_1, Button_2_left_hand.1
  N8: Bela1.P8_15_D8, R9.Pin_1, Button_1_right_hand.1
  N9: Bela1.P8_16_D9, R8.Pin_1, Button_2_right_hand.1
  GND: Bela1.P9_01_GND, Accelerometer_Left_Hand.GND, Accelerometer_Right_Hand.GND
  N10: Bela1.P9_02_GND, Trill_Craft1.GND
  N11: Bela1.P9_03_3.3V, Trill_Craft1.VCC, Button_1_left_hand.2, Button_2_left_hand.2, Button_1_right_hand.2, Button_2_right_hand.2
  VCC: Bela1.P9_04_3.3V, Accelerometer_Left_Hand.VCC, Accelerometer_Right_Hand.VCC
  N12: Bela1.P9_15_I2C_SCL, Trill_Craft1.SCL
  N13: Bela1.P9_18_I2C_SDA, Trill_Craft1.SDA
  N14: Bela1.AIN_5, Accelerometer_Left_Hand.ZOUT
  N15: Bela1.AIN_4, Accelerometer_Left_Hand.YOUT
  N16: Bela1.AIN_3, Accelerometer_Left_Hand.XOUT
  N17: Bela1.AIN_2, Accelerometer_Right_Hand.ZOUT
  N18: Bela1.AIN_1, Accelerometer_Right_Hand.YOUT
  N19: Bela1.AIN_0, Accelerometer_Right_Hand.XOUT
  N20: Trill_Craft1.0, Capacitive_Sensor_1.antenna_lead
  N21: Trill_Craft1.1, Capacitive_Sensor_2.antenna_lead
  N22: Trill_Craft1.2, Capacitive_Sensor_3.antenna_lead
  N23: Trill_Craft1.3, Capacitive_Sensor_4.antenna_lead
  N24: Trill_Craft1.4, Capacitive_Sensor_5.antenna_lead
  N25: Trill_Craft1.5, Capacitive_Sensor_6.antenna_lead
  N26: Trill_Craft1.6, Capacitive_Sensor_7.antenna_lead
  N27: Trill_Craft1.7, Capacitive_Sensor_8.antenna_lead
  N28: Trill_Craft1.8, Capacitive_Sensor_9.antenna_lead
  N29: Trill_Craft1.9, Capacitive_Sensor_10.antenna_lead
  N30: Trill_Craft1.10, Capacitive_Sensor_11.antenna_lead
  N31: Trill_Craft1.11, Capacitive_Sensor_12.antenna_lead
  N32: Trill_Craft1.12, Capacitive_Sensor_13.antenna_lead
  N33: Trill_Craft1.13, Capacitive_Sensor_14.antenna_lead
  N34: Trill_Craft1.14, Capacitive_Sensor_15.antenna_lead
  N35: Trill_Craft1.15, Capacitive_Sensor_16.antenna_lead
  N36: LED4_right_hand.cathode, R3.Pin_0
  N37: LED3_right_hand.cathode, R5.Pin_0
  N38: LED2_left_hand.cathode, R7.Pin_0
  N39: LED1_left_hand.cathode, R6.Pin_0

custom parts:
  Bela: A Fritzing part for Bela
  Trill Craft: A 30-channel breakout board for building touch interfaces out of any conductive material, by Bela.io
